# Fritzing sketch horgaszcucc_panel (saved by Fritzing 0.9.6b)

parts:
  A2 = ESP32-S3 supermini
  S1 = Pushbutton [package="[THT]"]
  S2 = Pushbutton [package="[THT]"]
  Part1 = HX711 Weighing Sensor Module
  R1 = Resistor [tolerance=±5% power=0.25 resistance=220 package=THT]
  R2 = Resistor [tolerance=±5% power=0.25 resistance=220 package=THT]
  Load_Cell1 = Load Cell - Red/white/black/green
  Squix1 = OLED 0.91" 128x32 I2C SSD1306 (GND/VCC)

nets:
  N1: A2.Pin_5, Squix1.SCA
  N2: A2.Pin_6, Squix1.SCL
  N3: A2.Pin_7, Part1.DO/RX
  N4: A2.Pin_8, Part1.CK/TX
  N5: A2.Pin_9, S2.Pin_3, R2.Pin_1
  N6: A2.Pin_10, S1.Pin_3, R1.Pin_1
  GND: A2.Pin_39, S1.Pin_1, S1.Pin_2, S2.Pin_1, S2.Pin_2, Part1.GND, Squix1.GND
  5V: A2.Pin_40, Part1.VCC, R1.Pin_0, R2.Pin_0, Squix1.VCC
  N7: Part1.E+, Load_Cell1.wire1
  N8: Part1.E-, Load_Cell1.wire3
  N9: Part1.A+, Load_Cell1.wire4
  N10: Part1.A-, Load_Cell1.wire2

notes:
  HX711
  Load Cell
  0.91inc Oled Display
  ESP32S3

custom parts:
  ESP32-S3 supermini: Esp32-S3 Development board ESP32 SuperMini development board ESP32 Development board WiFi Bluetooth.
  HX711 Weighing Sensor Module: HX711 is a precision 24-bit analog-to-digital converter (ADC) designed for weigh scales and industrial control applications to interface directly with a bridge sensor.
  Load Cell - Red/white/black/green: A rectangle load cell/weighting pressure Sensor with four wires - Red, white, black, green. Normally corresponding with E+, E-, A+, A- respectively.
  OLED 0.91" 128x32 I2C SSD1306 (GND/VCC): OLED 0.91" 128x32 I2C SSD1306 Pinout: GND/VCC/SCL/SDA
